# Fritzing sketch pico-xmas (saved by Fritzing 1.0.1rc)
breadboards: 3

parts:
  S1 = Pushbutton [package="[SMD]"]
  Mod1 = Raspberry Pi Pico
  S2 = Pushbutton [package="[SMD]"]
  SW1 = DIP SWITCH [package=dipswitch-02]
  SW2 = DIP SWITCH [package=dipswitch-02]
  SW3 = DIP SWITCH [package=dipswitch-02]
  LED1 = RGB LED (com. cathode, rgb) [color="Red (633nm)" current=0.030A package="5 mm [THT]"]
  LED2 = RGB LED (com. cathode, rgb) [color="Red (633nm)" current=0.030A package="5 mm [THT]"]

nets:
  N1: S1.Pin_1, S1.Pin_2, Mod1.pin_36, S2.Pin_1, S2.Pin_2, SW1.1, SW1.2, SW2.1, SW2.2, SW3.1, SW3.2
  N2: S1.Pin_3, S1.Pin_4, Mod1.pin_1
  N3: Mod1.pin_2, S2.Pin_3, S2.Pin_4
  N4: Mod1.pin_3, Mod1.pin_8, Mod1.pin_13, Mod1.pin_18, Mod1.pin_23, Mod1.pin_28, Mod1.pin_33, Mod1.pin_38, LED1.common_cathode, LED2.common_cathode
  N5: Mod1.pin_4, SW1.4
  N6: Mod1.pin_5, SW1.3
  N7: Mod1.pin_6, SW2.4
  N8: Mod1.pin_7, SW2.3, SW3.4
  N9: Mod1.pin_9, SW3.3
  N10: Mod1.pin_32, LED2.red_anode
  N11: Mod1.pin_34, LED1.red_anode
  N12: Mod1.pin_40, LED1.blue_anode, LED2.blue_anode

custom parts:
  Raspberry Pi Pico: Raspberry Pi Pico. Based around the RP2040 microcontroller the Pico is a low cost microcontroller device bringing Raspberry Pi quality, cost, and easy of use to the microcontroller space. Jan 2021, Split part in to two versions: tht (this one) and SMD. This one will drill holes for a .1 in header in pcb to allow plugging in the module as well as providing pads to solder the module to the top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
